# Fritzing sketch Circuito_invernadero (saved by Fritzing 0.9.3b)
breadboards: 1

parts:
  LCD_I2C = LCD1602-I2C
  FC-28_1 = FC-28 Soil Hygrometer Module
  Probe_1 = FC-28 Soil Hygrometer Module - Probe
  Arduino_UNO = Arduino Uno (Rev3)
  S1 = Pushbutton [package="[THT]"]
  S2 = Pushbutton [package="[THT]"]
  U1 = Module 4 Relais 5V [package="Module 4 Relais 5V"]
  R1 = Rotary Potentiometer (Small) [maximum_resistance=100kΩ package=THT]
  R2 = Resistor [tolerance=±5% resistance=1k package=THT]
  R3 = Resistor [tolerance=±5% resistance=1k package=THT]
  FC-28_2 = FC-28 Soil Hygrometer Module
  Probe_2 = FC-28 Soil Hygrometer Module - Probe
  FC-28_3 = FC-28 Soil Hygrometer Module
  Probe_3 = FC-28 Soil Hygrometer Module - Probe
  R4 = Resistor [tolerance=±5% resistance=10k package=THT]
  R5 = Photocell (LDR) [package=THT]
  U2 = SWITCH_SPDT [package=kps-1290]
  R6 = Resistor [tolerance=±5% resistance=1k package=THT]
  U3 = Module 4 Relais 5V [package="Module 4 Relais 5V"]
  DHT11 = DHT11 Humitidy and Temperature Sensor (3 pins)

nets:
  GND: LCD_I2C.GND, FC-28_1.GND, Arduino_UNO.GND, U1.GND, R1.leg1, R2.Pin_0, R3.Pin_0, FC-28_2.GND, FC-28_3.GND, R4.Pin_0, R6.Pin_0, U3.GND, DHT11.Gnd
  VCC: LCD_I2C.VCC, FC-28_1.VCC, Arduino_UNO.5V, S1.Pin_3, S1.Pin_4, S2.Pin_3, S2.Pin_4, U1.VCC, R1.leg2, FC-28_2.VCC, FC-28_3.VCC, R5.pin_0, U2.P, U3.VCC, DHT11.Plus
  N1: LCD_I2C.SDA, Arduino_UNO.A4/SDA
  N2: LCD_I2C.SCL, Arduino_UNO.A5/SCL
  N3: FC-28_1.AO, Arduino_UNO.A2
  N4: FC-28_1.POS, Probe_1.POS
  N5: FC-28_1.NEG, Probe_1.NEG
  N6: Arduino_UNO.A0, FC-28_2.AO
  N7: Arduino_UNO.A1, FC-28_3.AO
  N8: Arduino_UNO.A3, R1.wiper
  N9: Arduino_UNO.D8, U3.IN1
  N10: Arduino_UNO.D9_PWM, DHT11.Signal
  N11: Arduino_UNO.D10_PWM/SS, U1.IN4
  N12: Arduino_UNO.D11_PWM/MOSI, U1.IN3
  N13: Arduino_UNO.D12/MISO, U1.IN2
  N14: Arduino_UNO.D13/SCK, U1.IN1
  N15: Arduino_UNO.D2, S2.Pin_1, S2.Pin_2, R2.Pin_1
  N16: Arduino_UNO.D3_PWM, S1.Pin_1, S1.Pin_2, R3.Pin_1
  N17: Arduino_UNO.D4, R4.Pin_1, R5.pin_1
  N18: Arduino_UNO.D5_PWM, U2.O, R6.Pin_1
  N19: Arduino_UNO.D6_PWM, U3.IN3
  N20: Arduino_UNO.D7, U3.IN2
  N21: FC-28_2.POS, Probe_2.POS
  N22: FC-28_2.NEG, Probe_2.NEG
  N23: FC-28_3.POS, Probe_3.POS
  N24: FC-28_3.NEG, Probe_3.NEG

custom parts:
  LCD1602-I2C: A standard character display, usually with 2x16 characters. Comes in many colors with LCM1602 IIC attached.
  FC-28 Soil Hygrometer Module: The FC-28 is a soil hygrometer module that uses the Texas Instruments LM393 comparator chip to provide an analog measurement of soil humidity. The digital output is high when soil moisture is over a certain threshold, as determined by adjusting the potentiometer.
  FC-28 Soil Hygrometer Module - Probe: The FC-28 is a soil hygrometer module that uses the Texas Instruments LM393 comparator chip to provide an analog measurement of soil humidity.
  Module 4 Relais 5V: Module 4 Relais 5V 4x SPD-06VDC-SD-C
  DHT11 Humitidy and Temperature Sensor (3 pins): DHT11 Humidity and Temperature Sensor (3 pins).
